# Fritzing sketch greenhouse (saved by Fritzing 0.9.3b)
breadboards: 1

parts:
  Part1 = Arduino Uno (Rev3)
  RHT1 = Humidity and Temperature Sensor RHT03
  R1 = Resistor [tolerance=±5% resistance=10k package=THT]
  KY-1 = Keyes Relay [package=THT]
  KY-2 = Keyes Relay [package=THT]
  LED1 = Super Flux LED blue [color=Blue]
  Part2 = Real Time Clock Module - DS1307 RTC Breakout Board

nets:
  N1: Part1.A4/SDA, Part2.SDA
  N2: Part1.A5/SCL, Part2.SCL
  N3: Part1.D2, RHT1.Data-signal, R1.Pin_1
  N4: Part1.D3_PWM, KY-1.signal
  N5: Part1.D7, KY-2.signal
  5V: Part1.5V, RHT1.Vcc, R1.Pin_0, KY-1.power, KY-2.power, Part2.5V
  GND: Part1.GND, RHT1.GND_2, KY-1.ground, KY-2.ground, LED1.cathode, Part2.GND
  N6: KY-2.NO, LED1.anode

custom parts:
  Keyes Relay: The Keyes 5V relay module is suitable for SCM development, home appliance control. It uses a 5V~12V TIL control signal which can control DC / AC signal.

// code stored in the sketch: greenhouse.ino
#include "DHT.h"
#include "iarduino_RTC.h"

#define DHTPIN 2     // what digital pin we're connected to
// Uncomment whatever type you're using!
//#define DHTTYPE DHT11   // DHT 11
#define DHTTYPE DHT22   // DHT 22  (AM2302), AM2321
//#define DHTTYPE DHT21   // DHT 21 (AM2301)
iarduino_RTC time(RTC_DS1307);
DHT dht(DHTPIN, DHTTYPE);
//Application constants and variables
#define MIN_TEMP 14 // temperature for switch on heater 
#define MAX_TEMP 18 // temperature for switch off heater
#define HEATER_PIN 3 //pin for heater reley module
#define LIGHT_PIN 7 //pin for light relay module
boolean isHeaterOn;
boolean isLightOn;

void setup() {
  Serial.begin(9600);
  Serial.println("DHTxx test!");
	pinMode(HEATER_PIN, OUTPUT);
	digitalWrite(HEATER_PIN, LOW);
	isHeaterOn = false;
	pinMode(LIGHT_PIN, OUTPUT);
	digitalWrite(LIGHT_PIN, LOW);
	isLightOn = false;
	time.begin();
  dht.begin();
	//time.settime(0,51,21,20,10,18,6);
}

void loop() {
  // Wait a few seconds between measurements.
  delay(2000);

  float t = dht.readTemperature();

  // Check if any reads failed and exit early (to try again).
  if (isnan(t)) {
    Serial.println("Failed to read from DHT sensor!");
    return;
  }
	if(t < MIN_TEMP && !isHeaterOn)
	{
		Serial.println("Heater on!");
		isHeaterOn = true;
		digitalWrite(HEATER_PIN, HIGH);
	}
	if(t > MAX_TEMP && isHeaterOn)
	{
		Serial.println("Heater off!");
		isHeaterOn = false;	
		digitalWrite(HEATER_PIN, LOW);
	}
	int hours = time.getTime("H");
	if( hours > 17 && hours <22 && !isLightOn )
	{
		Serial.println("Light on!");
		isLightOn = true;
		digitalWrite(LIGHT_PIN, HIGH);
	}
	if( hours > 5 && hours < 8 && !isLightOn )
	{
		Serial.println("Light on!");
		isLightOn = true;
		digitalWrite(LIGHT_PIN, HIGH);
	}
	if( hours > 22 && isLightOn )
	{
		Serial.println("Light off!");
		isLightOn = false;
		digitalWrite(LIGHT_PIN, LOW);
	}
	if( hours > 8 && hours < 17 && isLightOn )
	{
		Serial.println("Light off!");
		isLightOn = false;
		digitalWrite(LIGHT_PIN, LOW);
	}
}

